# Fritzing sketch esquema (saved by Fritzing 0.9.3b)
breadboards: 3

parts:
  Componente1 = Arduino Uno (Rev3)
  LCD1 = LCD screen
  S1 = Pushbutton [package="[SMD]"]
  S2 = Pushbutton [package="[SMD]"]
  S3 = Pushbutton [package="[SMD]"]
  R1 = Resistor [tolerance=±5% resistance=1k package=THT]
  R2 = Resistor [tolerance=±5% resistance=1k package=THT]
  R3 = Resistor [tolerance=±5% resistance=1k package=THT]
  R4 = Resistor [tolerance=±5% resistance=1k package=THT]
  R5 = Resistor [tolerance=±5% resistance=1k package=THT]
  J1 = Piezo Speaker
  R6 = Resistor [tolerance=±5% resistance=1k package=THT]
  S4 = Round Pushbutton
  LED1 = smd LED [color="Green (560nm)" package="1206 [SMD]"]
  R7 = Trimmer Potentiometer [maximum_resistance=10kΩ package=THT]

nets:
  N1: Componente1.A5/SCL, R3.Pin_1, R4.Pin_1
  N2: Componente1.D8, LCD1.RS
  N3: Componente1.D9_PWM, R6.Pin_0, S4.leg0
  N4: Componente1.D12/MISO, J1.pin2
  5V: Componente1.D13/SCK, Componente1.5V, LCD1.VDD, LCD1.LED+, S1.Pin_1, S1.Pin_2, S2.Pin_1, S2.Pin_2, S3.Pin_1, S3.Pin_2, R5.Pin_1, LED1.anode
  GND: Componente1.GND, LCD1.VSS, LCD1.R/W, LCD1.LED-, R4.Pin_0, R5.Pin_0, J1.pin1, R6.Pin_1, R7.leg2
  N5: Componente1.D2, LCD1.E
  N6: Componente1.D4, LCD1.DB4
  N7: Componente1.D5_PWM, LCD1.DB5
  N8: Componente1.D6_PWM, LCD1.DB6
  N9: Componente1.D7, LCD1.DB7
  N10: S1.Pin_3, S1.Pin_4, R1.Pin_0
  N11: S2.Pin_3, S2.Pin_4, R1.Pin_1, R2.Pin_0
  N12: S3.Pin_3, S3.Pin_4, R2.Pin_1, R3.Pin_0
  N13: S4.leg1, LED1.cathode

notes:
  MAPA
